# Fritzing sketch poolMCU (saved by Fritzing 0.9.3b)
breadboards: 1

parts:
  Q1 = NPN-Transistor [package="TO92 [THT]"]
  Q2 = NPN-Transistor [package="TO92 [THT]"]
  Q3 = NPN-Transistor [package="TO92 [THT]"]
  U1 = NodeMCU V1.0
  R1 = Resistor [tolerance=±1% resistance=10k package="2512 [SMD]"]
  JP1 = Header 6 [package=molex-1x6-ra]
  JP2 = Header 6 [package=molex-1x6-ra]
  JP3 = Header 4 [package=screwterminal-3.5mm-4_lock]

nets:
  N1: Q1.E, Q2.E, Q3.E, JP1.1
  N2: Q1.B, U1.D6
  N3: Q1.C, JP1.5
  N4: Q2.B, U1.D7
  N5: Q2.C, JP1.4
  N6: Q3.B, U1.D8
  N7: Q3.C, JP1.3
  N8: U1.D0, JP2.2
  N9: U1.GND, R1.Pin_0, JP3.1
  N10: U1.D5, R1.Pin_1, JP1.2
  N11: U1.Vin, JP3.4

custom parts:
  NodeMCU V1.0: ESP8266 based NodeMCU
